// Logisim project MIPS Project.circ as structural Verilog
module IM (
  input  [5:0] in_1,
  output [3:0] Shft_Amnt__0_3,
  output [3:0] Dst_Reg_4_7,
  output [3:0] Src_Reg_2__8_11,
  output [3:0] Src_Reg_1_12_15,
  output [3:0] Opcode_19_16,
  output [7:0] Add_Immi_0_7,
  output [7:0] Jump__8_15
);

  ROM #(.addrWidth(6), .dataWidth(20)) rom_1 (
    .addr(in_1), .data({Jump__8_15[7:4], Jump__8_15, Add_Immi_0_7}));  // open: sel

  assign Dst_Reg_4_7 = Add_Immi_0_7[7:4];
  assign Opcode_19_16 = Jump__8_15[7:4];
  assign Shft_Amnt__0_3 = Add_Immi_0_7[3:0];
  assign Src_Reg_1_12_15 = Jump__8_15[7:4];
  assign Src_Reg_2__8_11 = Jump__8_15[3:0];
endmodule

module DM (
  input  [7:0] Address,
  input  [7:0] Data,
  input  Store,
  input  Select,
  input  Load,
  input  Clear,
  output [7:0] Loaded_Data
);

  wire Clock_out;

  Clock Clock (.out(Clock_out));
  RAM #(.bus("separate")) ram_1 (
    .addr(Address), .din(Data), .data(Loaded_Data), .str(Store), .sel(Select), .clk(Clock_out), .ld(Load),
    .clr(Clear));
endmodule

module Register_File (
  input  [3:0] ReadReg_1,
  input  [3:0] ReadReg_2,
  input  [7:0] Data,
  input  [3:0] Write_Reg_Addr,
  input  Write_Signal,
  input  Clear,
  output [7:0] ReadData_1,
  output [7:0] ReadData_2,
  output [7:0] Zero,
  output [7:0] t0,
  output [7:0] t1,
  output [7:0] t2,
  output [7:0] t3,
  output [7:0] t4,
  output [7:0] SP
);

  wire and_1_out, and_2_out, and_3_out, and_4_out, and_5_out, and_6_out, and_7_out, Clock_out,
       decoder_1_out0, decoder_1_out1, decoder_1_out2, decoder_1_out3, decoder_1_out4, decoder_1_out5,
       decoder_1_out6, multiplexer_2_out, multiplexer_3_out;
  wire [7:0] multiplexer_1_out;

  Decoder #(.select(4)) decoder_1 (
    .out0(decoder_1_out0), .out1(decoder_1_out1), .out2(decoder_1_out2), .out3(decoder_1_out3),
    .out4(decoder_1_out4), .out5(decoder_1_out5), .out6(decoder_1_out6), .sel(Write_Reg_Addr));  // open: out7, out8, out9, out10, out11, out12, out13, out14, out15, en
  and and_1 (and_1_out, decoder_1_out0, 1'b0);
  and and_2 (and_2_out, decoder_1_out1, Write_Signal);
  and and_3 (and_3_out, decoder_1_out2, Write_Signal);
  and and_4 (and_4_out, decoder_1_out3, Write_Signal);
  and and_5 (and_5_out, decoder_1_out4, Write_Signal);
  and and_6 (and_6_out, decoder_1_out5, Write_Signal);
  and and_7 (and_7_out, decoder_1_out6, Write_Signal);
  Multiplexer #(.width(8)) multiplexer_1 (
    .in0(Data), .in1({8{1'b1}}), .out(multiplexer_1_out), .sel(Clear));  // open: en
  Multiplexer multiplexer_2 (.in0(and_7_out), .in1(Clear), .out(multiplexer_2_out), .sel(Clear));  // open: en
  Multiplexer multiplexer_3 (.in0(Clock_out), .in1(Clear), .out(multiplexer_3_out), .sel(Clear));  // open: en
  Clock Clock (.out(Clock_out));
  Register register_1 (.D(Data), .en(and_1_out), .Q(Zero), .clk(Clock_out), .clr(Clear));
  Register register_2 (.D(Data), .en(and_2_out), .Q(t0), .clk(Clock_out), .clr(Clear));
  Register register_3 (.D(Data), .en(and_3_out), .Q(t1), .clk(Clock_out), .clr(Clear));
  Register register_4 (.D(Data), .en(and_4_out), .Q(t2), .clk(Clock_out), .clr(Clear));
  Register register_5 (.D(Data), .en(and_5_out), .Q(t3), .clk(Clock_out), .clr(Clear));
  Register register_6 (.D(Data), .en(and_6_out), .Q(t4), .clk(Clock_out), .clr(Clear));
  Register register_7 (.D(multiplexer_1_out), .en(multiplexer_2_out), .Q(SP), .clk(multiplexer_3_out));  // open: clr
  Multiplexer #(.select(4), .width(8)) multiplexer_4 (
    .in0(Zero), .in1(t0), .in2(t1), .in3(t2), .in4(t3), .in5(t4), .in6(SP), .out(ReadData_1), .sel(ReadReg_1));  // open: in7, in8, in9, in10, in11, in12, in13, in14, in15, en
  Multiplexer #(.select(4), .width(8)) multiplexer_5 (
    .in0(Zero), .in1(t0), .in2(t1), .in3(t2), .in4(t3), .in5(t4), .in6(SP), .out(ReadData_2), .sel(ReadReg_2));  // open: in7, in8, in9, in10, in11, in12, in13, in14, in15, en

  // Notes on the sheet:
  //   Zero
  //   t0
  //   t1
  //   t2
  //   t3
  //   t4
  //   SP
endmodule

module Control_Unit (
  input  [3:0] OpCode,
  output [2:0] ALUOp,
  output ALUSrc,
  output Shift,
  output Jump,
  output beq,
  output bneq,
  output RegDest,
  output RegWrite,
  output MemRead,
  output MemWrite,
  output MemToReg
);

  ROM #(.addrWidth(4), .dataWidth(13)) rom_1 (
    .addr(OpCode),
    .data({MemToReg, MemWrite, MemRead, RegWrite, RegDest, bneq, beq, Jump, Shift, ALUSrc, ALUOp}));  // open: sel

  // Notes on the sheet:
  //   contents of rom_1 (hex, n*v repeats v):
  //   41 21 303 81 302 301 316 209 20b 20a 208 808 300 1608 304 315
endmodule
